# Fritzing sketch plant light one diode (saved by Fritzing 0.8.7b)
breadboards: 1

parts:
  Part2 = Arduino BT
  LCD1 = LCD screen
  R1 = PHOTOCELL [package=photocell-kit]
  R2 = Resistor [tolerance=±5% resistance=220 package=THT]

nets:
  N1: Part2.GND, LCD1.RS, R2.Pin_1
  N2: Part2.A4/SDA, LCD1.VDD
  N3: Part2.A5/SCL, LCD1.VSS
  N4: Part2.A0, R1.P$2, R2.Pin_0
  N5: Part2.5V, LCD1.V0, R1.P$1
