# Fritzing sketch plant light two diodes (saved by Fritzing 0.8.7b)
circuit board: 6.88566cm x 5.36311cm
breadboards: 1

parts:
  R5 = Photocell (LDR) [package=THT]
  R6 = Resistor [tolerance=±5% resistance=10k package=THT]
  R7 = Photocell (LDR) [package=THT]
  R8 = Resistor [tolerance=±5% resistance=10k package=THT]
  Arduino1 = Arduino Uno (Rev3)

nets (from the breadboard view):
  N1: R5.pin_0, R7.pin_0, Arduino1.5V
  N2: R5.pin_1, R6.Pin_0, Arduino1.A0
  N3: R6.Pin_1, R8.Pin_1, Arduino1.GND
  N4: R7.pin_1, R8.Pin_0, Arduino1.A1
